# Fritzing sketch Sampler (saved by Fritzing 0.9.3b)

parts:
  Power_plug1 = Power plug
  U2 = Voltage Regulator - Variable [package="TO220 [THT]"]
  U1 = Voltage Regulator - Variable [package="TO220 [THT]"]
  M1 = DC Motor  # not connected
  Raspberry_Pi_Zero1 = Raspberry Pi Zero
  JP1 = USB_MICROB_PLUG [package=micro-b-ra-th]
  M2 = DC Motor  # not connected
  M3 = DC Motor  # not connected
  M4 = DC Motor  # not connected
  J1 = female pin header, 5 pins [form="♀ (female)"]
  J2 = female pin header, 2 pins [form="♀ (female)"]
  J3 = female pin header, 5 pins [form="♀ (female)"]
  J4 = female pin header, 5 pins [form="♀ (female)"]
  J5 = female pin header, 5 pins [form="♀ (female)"]
  J6 = female pin header, 5 pins [form="♀ (female)"]
  J7 = female pin header, 2 pins [form="♀ (female)"]
  J8 = female pin header, 2 pins [form="♀ (female)"]
  J9 = female pin header, 2 pins [form="♀ (female)"]

nets:
  GND: Power_plug1.GND, U2.OUT, U1.OUT, JP1.GND, J2.pin1, J7.pin1, J8.pin1, J9.pin1
  N1: Power_plug1.VCC, U2.ADJ, U1.ADJ
  N2: U2.IN, JP1.VCC
  N3: U1.IN, J2.pin2, J7.pin2, J8.pin2, J9.pin2
  3V3: Raspberry_Pi_Zero1.3v3, Raspberry_Pi_Zero1.3V3, J1.pin2, J3.pin2, J4.pin2, J5.pin2, J6.pin2
  N4: Raspberry_Pi_Zero1.GPIO2, J1.pin4, J3.pin4, J4.pin4, J5.pin4, J6.pin4
  N5: Raspberry_Pi_Zero1.GPIO3, J1.pin5, J3.pin5, J4.pin5, J5.pin5, J6.pin5
  N6: Raspberry_Pi_Zero1.GND, J1.pin3, J3.pin3, J4.pin3, J5.pin3, J6.pin3
  N7: J1.pin1, J3.pin1, J4.pin1, J5.pin1, J6.pin1

notes:
  12V UBEC
  5V UBEC
  AtlasScientific's EZO-PMP
  S4 Battery
  Cables:
  Blue - INT
  Red - VCC
  Black - GND
  Green - SDA
  White - SCL
